# Fritzing sketch DonationBox (saved by Fritzing 0.9.2b)
breadboards: 1

parts:
  U1 = attiny85 [package=dip]
  Part1 = Thermal Printer
  Raspberry_Pi1 = Raspberry Pi 2
  S1 = Square Pushbutton
  J1 = Power Jack [package=power_jack_combo]
  Power_plug1 = Power plug  # not connected
  CONN1 = USB connector [package=THT]
  R1 = Resistor [tolerance=±5% resistance=220 package=THT]
  C1 = Electrolytic Capacitor [capacitance=1µF package="100 mil [THT, electrolytic]"]
  R2 = Resistor [tolerance=±5% resistance=220 package=THT]

nets:
  N1: U1.Pin_2, CONN1.d-
  N2: U1.Pin_3, CONN1.d+
  GND: U1.Pin_4, Part1.GND#0, Raspberry_Pi1.GND, S1.leg1, J1.GND, C1.-
  N3: Part1.VH, J1.PWR
  N4: Part1.RXD, Raspberry_Pi1.GPIO14
  N5: Raspberry_Pi1.GPIO21, R1.Pin_1, C1.+, R2.Pin_1
  N6: Raspberry_Pi1.5V, R1.Pin_0
  N7: S1.leg0, R2.Pin_0

notes:
  Coin Acceptor Rx
  USB to Raspberry Pi
  9V 1.5A - Printer
  12V - Coin Acceptor
  Raspberry Pi - Shutdown
